# Fritzing sketch arduino-sensors (saved by Fritzing 0.9.4)
breadboards: 1

parts:
  Part1 = Arduino Leonardo (Rev3b)
  BME280 = BMP280
  Cds = PHOTOCELL [package=photocell]
  R1 = Resistor [tolerance=±5% resistance=10k package=THT]

nets:
  N1: Part1.D2/SDA, BME280.SDA
  N2: Part1.D3_PWM/SCL, BME280.SCL
  5V: Part1.5V, BME280.VIN, R1.Pin_1
  GND: Part1.GND, BME280.GND, Cds.P$1
  N3: Part1.A0, Cds.P$2, R1.Pin_0

custom parts:
  BMP280: Temperature Humidity Barometric presure Sensor, I2C

// code stored in the sketch: BME-BMP280_Arduino_test.ino
//BMP280 test
#include <Wire.h>
#include <Adafruit_Sensor.h>
#include <Adafruit_BME280.h>
#define SEALEVELPRESSURE_HPA (1013.25)
Adafruit_BME280 bme;
void setup() {
  Serial.begin(9600);
  if (!bme.begin(0x76)) {
    Serial.println("Could not find a valid BME280 sensor, check wiring!");
    while (1);
  }
  Serial.print("Hello");
}
void loop() {
  //Serial.print("Temperature = ");
  Serial.print(bme.readTemperature());
  Serial.print("*C  ");
  //Serial.print("Pressure = ");
  Serial.print(bme.readPressure() / 100.0F);
  Serial.print("hPa  ");
  //Serial.print("Humidity = ");
  Serial.print(bme.readHumidity());
  Serial.print("%  ");
  Serial.println();
  delay(1000);
}
